# Fritzing sketch Arduino-Diag (saved by Fritzing 0.9.8b)
breadboards: 1

parts:
  Part1 = Arduino Uno (Rev3)  # not connected
  Part3 = Arduino GSM Shield
  R2 = Photocell (LDR) [package=THT]
  R3 = Resistor [tolerance=±5% power=0.25 resistance=10k package=THT]
  RHT1 = Humidity and Temperature Sensor RHT03

nets:
  N1: Part3.A5/SCL, R2.pin_1, R3.Pin_1
  N2: Part3.D8, RHT1.Data-signal
  5V: Part3.5V, R2.pin_0, RHT1.Vcc
  N3: Part3.AGND, R3.Pin_0, RHT1.GND_2
